# Fritzing sketch Schematic (saved by Fritzing 0.9.4)

parts:
  U2 = LuaNode32 / ESP32
  Squix1 = OLED 0.91" 128x32 I2C SSD1306 (GND/VCC)  # not connected
  SIM800L_BO1 = SIM800L BO
  ZS-042_RTC1 = ZS-042 RTC Module  # not connected
  DC-DC_5_to_4_volt = DC-DC_CONVERTER [package=dc-dc_converter]
  1000_uF = Electrolytic Capacitor [capacitance=0pF voltage=16V package="100 mil [THT, electrolytic]"]
  R1 = Resistor [tolerance=±5% resistance=100k package=THT]
  R2 = Resistor [tolerance=±5% resistance=10k package=THT]
  microSD1 = MicroSD Card Module
  J1 = Power Jack [package=power_jack_smd]
  ANT1 = Antenna

nets:
  N1: U2.Vin, J1.GNDBREAK
  GND: U2.GND, J1.GND
  N2: U2.D2, R1.Pin_0
  N3: U2.D4, SIM800L_BO1.pin_5
  N4: U2.D5, microSD1.CS
  N5: U2.D18, microSD1.SCK
  N6: U2.D19, microSD1.MISO
  N7: U2.D23, microSD1.MOSI
  N8: SIM800L_BO1.PIN1, ANT1.antenna_lead
  N9: SIM800L_BO1.PIN2, DC-DC_5_to_4_volt.GND2, 1000_uF.+
  N10: SIM800L_BO1.pin_4, R2.Pin_0
  N11: SIM800L_BO1.pin_6, 1000_uF.-

notes:
  RX
  TX
  MISO
  MOSI
  SCK
  CS

custom parts:
  LuaNode32 / ESP32: ESP32 based LuaNode32
  OLED 0.91" 128x32 I2C SSD1306 (GND/VCC): OLED 0.91" 128x32 I2C SSD1306 Pinout: GND/VCC/SCL/SDA
